// Logisim project CPU.circ as structural Verilog: 3 circuits, main circuit main
module main (
  input  in_1,
  input  [7:0] in_2,
  input  in_3,
  input  in_4,
  input  in_5,
  input  in_6
);

  wire clk, hlt;
  wire [7:0] d_bus;

  Button stop (.out(hlt));
  LedBar ledbar_1 (
    .led0(d_bus[7]), .led1(d_bus[6]), .led2(d_bus[5]), .led3(d_bus[4]), .led4(d_bus[3]), .led5(d_bus[2]),
    .led6(d_bus[1]), .led7(d_bus[0]));
  cpu_clk cpu_clk_1 (.hlt(hlt), .clk(clk));
  gen_reg A (.d_bus(d_bus), .OE(in_3), .load(in_4), .clk(clk), .d_out(d_bus));
  gen_reg B (.d_bus(d_bus), .OE(in_5), .load(in_6), .clk(clk), .d_out(d_bus));
  assign d_bus = in_1 ? in_2 : 8'bz;  // Controlled_Buffer controlled_buffer_1
endmodule

module gen_reg (
  input  [7:0] d_bus,
  input  OE,
  input  load,
  input  clk,
  output [7:0] d_out
);

  wire [7:0] register_1_q;

  Register register_1 (.D(d_bus), .en(load), .clk(clk), .Q(register_1_q));  // open: clr
  assign d_out = OE ? register_1_q : 8'bz;  // Controlled_Buffer controlled_buffer_1
endmodule

module cpu_clk (
  input  hlt,
  output clk
);

  wire clock_1_out, not_1_out;

  Clock clock_1 (.out(clock_1_out));
  not not_1 (not_1_out, hlt);
  and and_1 (clk, clock_1_out, not_1_out);
endmodule
